# Fritzing sketch S3GPIO (saved by Fritzing 0.9.7b)

parts:
  Mod1 = Raspberry Pi 4B
  U1 = L9110 H-bridge module [part_number="L9110 H-bridge"]
  Part1 = SRF05 Ultrasonic Rangefinder
  M1 = DC Motor
  VCC1 = Battery

nets:
  3V3: Mod1.3V3, Part1.VCC
  GND: Mod1.GND, U1.GND, Part1.GND, VCC1.-
  N1: Mod1.GPIO14, U1.A-IA
  N2: Mod1.GPIO15, U1.A-IB
  N3: Mod1.GPIO17, Part1.Trig
  N4: Mod1.GPIO27, Part1.Echo
  N5: U1.VCC, VCC1.+
  N6: U1.MOTOR_A-A, M1.pin_2
  N7: U1.MOTOR_A-B, M1.pin_1

notes:
  HC-SR04-P
